# Fritzing sketch Schematic (saved by Fritzing 0.8.5b)
breadboards: 1

parts:
  Part1 = Arduino Uno (Rev3)
  DHT1 = DHT11 Humitidy and Temperature Sensor
  Part2 = Soil Moisture Sensor  # not connected

nets:
  N1: Part1.A0, DHT1.DATA
  GND: Part1.GND, DHT1.GND
  3V3: Part1.3V3, DHT1.VDD

notes:
  TODO: Make custom part for board!

custom parts:
  DHT11 Humitidy and Temperature Sensor: DHT11 Humidity and Temperature Sensor
